# Fritzing sketch LehDevPlayСХЕМА (saved by Fritzing 0.9.5d)

parts:
  A1 = Werner Rothschopf (modified to ESP32-S3-DevKitC dual USB by vanepp Aug 2024)
  uSD_holder1 = KCL microSD shield
  Mod1 = KY-023 Dual Axis Joystick Module [package="Breakout board"]
  S1 = Pushbutton [package="[THT]"]
  S2 = Pushbutton [package="[THT]"]
  S3 = Pushbutton [package="[THT]"]
  LED1 = LED - 5mm [color="Red (633nm)" package="5 mm [THT]"]
  R1 = Resistor [tolerance=±5% resistance=220 package=THT]
  TP1 = TP4056 [chip_label=TP4056 package="DIP (Dual Inline) [THT]"]
  J1 = female pin header, 2 pins [form="♀ (female)"]
  S4 = Toggle Switch [package=THT]
  AMP1 = PAM8403 6W Stereo Amplifier
  MIC1 = Microphone

nets:
  N1: A1.Pin_1, A1.Pin_2, uSD_holder1.3V3, R1.Pin_0
  N2: A1.Pin_4, Mod1.SW
  N3: A1.Pin_5, S1.Pin_1, S1.Pin_2
  N4: A1.Pin_6, S2.Pin_1
  N5: A1.Pin_7, S3.Pin_1
  N6: A1.Pin_10, AMP1.INPUTL
  N7: A1.Pin_17, uSD_holder1.MOSI
  N8: A1.Pin_18, uSD_holder1.CLK
  N9: A1.Pin_19, uSD_holder1.MISO
  N10: A1.Pin_20, uSD_holder1.CS
  N11: A1.Pin_21, Mod1.+5V
  N12: A1.Pin_22, A1.Pin_23, A1.Pin_24, A1.Pin_44, Mod1.GND, S1.Pin_3, S1.Pin_4, S2.Pin_3, S2.Pin_4, S3.Pin_3, S3.Pin_4, AMP1.POWER-, AMP1.INPUTG
  N13: A1.Pin_40, Mod1.VRy
  N14: A1.Pin_41, Mod1.VRx
  N15: uSD_holder1.GND, LED1.anode
  N16: TP1.pin4, J1.pin1, S4.L1
  N17: TP1.pin5, J1.pin2
  N18: AMP1.LOUT+, MIC1.pin2
  N19: AMP1.LOUT-, MIC1.pin1

notes:
  220
  + -
  Кнопка F
  Кнопка R
  Кнопка Back (назад)
  SD ридер
  ESP32-S3 Dev Module
  - + X Y SW
  Светодиод не обязателен,он просмто показывает состояние питания
  - +
  + -
  АКБ(800-1500MAH)
  Динамик до 3W
  Игровая консоль LehDev Play!
  lehdev.mozellosite.com
  TG: @LehDev

custom parts:
  Werner Rothschopf (modified to ESP32-S3-DevKitC dual USB by vanepp Aug 2024): ESP32-S3 ESP32-S3-DevKitC-1 Dual USB development board Pyboard CircuitPython Micropython wifi BLE5.0 ESP32-S3.
  KCL microSD shield: KCL microSD shield Fritzing part for the commonly available mass-produced microSD card shields. MicroSD cards are inserted on the underside of the device with the connectors facing up. Creative Common Attribution 4.0 International (CC-BY 4.0) license. Any use of this part requires attribution of Dr Kristofer Chan, Department of Geography, King's College London. Contact kristofer.chan [at]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
  KY-023 Dual Axis Joystick Module: KY-023 Dual-Axis Joystick Module.
  TP4056: A DIP stand-in part for whatever IC you want. With 6 pins on a 300mil dual inline package (DIP) footprint.
  PAM8403 6W Stereo Amplifier: PAM8403 6 Watt Stereo Amplifier
